// Logisim project alu.circ as structural Verilog: 1 circuit, main circuit main
module main (
  input  x,
  input  zx,
  input  nx,
  input  y,
  input  zy,
  input  ny,
  input  f,
  input  no,
  output out_9
);

  wire and_1_out, and_2_out, and_3_out, and_4_out, and_5_out, not_1_out, not_2_out, not_3_out, or_1_out,
       xor_1_out, xor_2_out, xor_3_out;

  not not_1 (not_1_out, zx);
  not not_2 (not_2_out, zy);
  and and_1 (and_1_out, x, not_1_out);
  and and_2 (and_2_out, y, not_2_out);
  xor xor_1 (xor_1_out, and_1_out, nx);
  xor xor_2 (xor_2_out, and_2_out, ny);
  and and_3 (and_3_out, xor_1_out, xor_2_out);
  xor xor_3 (xor_3_out, xor_1_out, xor_2_out);
  not not_3 (not_3_out, f);
  and and_4 (and_4_out, and_3_out, not_3_out);
  and and_5 (and_5_out, xor_3_out, f);
  or or_1 (or_1_out, and_4_out, and_5_out);
  xor xor_4 (out_9, or_1_out, no);
endmodule
