// Logisim project alu3.circ as structural Verilog: 13 circuits, main circuit add16
module main (
  input  x_0,
  input  x_1,
  input  x_2,
  input  x_3,
  input  x_4,
  input  x_5,
  input  x_6,
  input  x_7,
  input  zx,
  input  nx,
  input  x_8,
  input  x_9,
  input  x_10,
  input  x_11,
  input  x_12,
  input  x_13,
  input  x_14,
  input  x_15,
  input  in_19,
  input  in_20,
  input  y_0,
  input  y_1,
  input  y_2,
  input  y_3,
  input  y_4,
  input  y_5,
  input  y_6,
  input  y_7,
  input  zy,
  input  ny,
  input  y_8,
  input  y_9,
  input  y_10,
  input  y_11,
  input  y_12,
  input  y_13,
  input  y_14,
  input  y_15,
  output zr,
  output ng
);

  wire alu1_1_out_0, alu1_1_out_1, alu1_1_out_2, alu1_1_out_3, alu1_1_out_4, alu1_1_out_5, alu1_1_out_6,
       alu1_1_out_7, alu1_1_out_8, alu1_1_out_9, alu1_1_out_10, alu1_1_out_11, alu1_1_out_12, alu1_1_out_13,
       alu1_1_out_14, alu1_1_out_15, or8way_1_out, or8way_2_out, or_1_out;

  alu1 alu1_1 (
    .x_0(x_0), .x_1(x_1), .x_2(x_2), .x_3(x_3), .x_4(x_4), .x_5(x_5), .x_6(x_6), .x_7(x_7), .zx(zx), .nx(nx),
    .x_8(x_8), .x_9(x_9), .x_10(x_10), .x_11(x_11), .x_12(x_12), .x_13(x_13), .x_14(x_14), .x_15(x_15),
    .f(in_19), .no(in_20), .y_0(y_0), .y_1(y_1), .y_2(y_2), .y_3(y_3), .y_4(y_4), .y_5(y_5), .y_6(y_6),
    .y_7(y_7), .zy(zy), .ny(ny), .y_8(y_8), .y_9(y_9), .y_10(y_10), .y_11(y_11), .y_12(y_12), .y_13(y_13),
    .y_14(y_14), .y_15(y_15), .out_0(alu1_1_out_0), .out_1(alu1_1_out_1), .out_2(alu1_1_out_2),
    .out_3(alu1_1_out_3), .out_4(alu1_1_out_4), .out_5(alu1_1_out_5), .out_6(alu1_1_out_6),
    .out_7(alu1_1_out_7), .out_8(alu1_1_out_8), .out_9(alu1_1_out_9), .out_10(alu1_1_out_10),
    .out_11(alu1_1_out_11), .out_12(alu1_1_out_12), .out_13(alu1_1_out_13), .out_14(alu1_1_out_14),
    .out_15(alu1_1_out_15));
  or8way or8way_1 (
    .in_0(alu1_1_out_0), .in_1(alu1_1_out_1), .in_2(alu1_1_out_2), .in_3(alu1_1_out_3), .in_4(alu1_1_out_4),
    .in_5(alu1_1_out_5), .in_6(alu1_1_out_6), .in_7(alu1_1_out_7), .out(or8way_1_out));
  or8way or8way_2 (
    .in_0(alu1_1_out_8), .in_1(alu1_1_out_9), .in_2(alu1_1_out_10), .in_3(alu1_1_out_11),
    .in_4(alu1_1_out_12), .in_5(alu1_1_out_13), .in_6(alu1_1_out_14), .in_7(alu1_1_out_15), .out(or8way_2_out));
  and and_1 (ng, alu1_1_out_15, 1'b1);
  or or_1 (or_1_out, or8way_1_out, or8way_2_out);
  not not_1 (zr, or_1_out);
endmodule

module mux (
  input  a,
  input  b,
  input  sel,
  output out_4
);

  wire and_1_out, and_2_out, not_1_out;

  not not_1 (not_1_out, sel);
  and and_1 (and_1_out, a, not_1_out);
  and and_2 (and_2_out, b, sel);
  or or_1 (out_4, and_1_out, and_2_out);
endmodule

module mux4 (
  input  a_0,
  input  b_0,
  input  a_1,
  input  b_1,
  input  sel,
  input  a_2,
  input  b_2,
  input  a_3,
  input  b_3,
  output out_10,
  output out_11,
  output out_12,
  output out_13
);

  mux mux_1 (.a(a_0), .b(b_0), .sel(sel), .out_4(out_10));
  mux mux_2 (.a(a_1), .b(b_1), .sel(sel), .out_4(out_11));
  mux mux_3 (.a(a_2), .b(b_2), .sel(sel), .out_4(out_12));
  mux mux_4 (.a(a_3), .b(b_3), .sel(sel), .out_4(out_13));
endmodule

module mux16 (
  input  a_0,
  input  b_0,
  input  a_1,
  input  b_1,
  input  a_2,
  input  b_2,
  input  a_3,
  input  b_3,
  input  a_4,
  input  b_4,
  input  a_5,
  input  b_5,
  input  a_6,
  input  b_6,
  input  a_7,
  input  b_7,
  input  a_8,
  input  b_8,
  input  a_9,
  input  b_9,
  input  a_10,
  input  b_10,
  input  a_11,
  input  b_11,
  input  a_12,
  input  b_12,
  input  a_13,
  input  b_13,
  input  a_14,
  input  b_14,
  input  a_15,
  input  b_15,
  input  sel,
  output out_0,
  output out_1,
  output out_2,
  output out_3,
  output out_4,
  output out_5,
  output out_6,
  output out_7,
  output out_8,
  output out_9,
  output out_10,
  output out_11,
  output out_12,
  output out_13,
  output out_14,
  output out_15
);

  mux4 mux4_1 (
    .a_0(a_0), .b_0(b_0), .a_1(a_1), .b_1(b_1), .sel(sel), .a_2(a_2), .b_2(b_2), .a_3(a_3), .b_3(b_3),
    .out_10(out_0), .out_11(out_1), .out_12(out_2), .out_13(out_3));
  mux4 mux4_2 (
    .a_0(a_4), .b_0(b_4), .a_1(a_5), .b_1(b_5), .sel(sel), .a_2(a_6), .b_2(b_6), .a_3(a_7), .b_3(b_7),
    .out_10(out_4), .out_11(out_5), .out_12(out_6), .out_13(out_7));
  mux4 mux4_3 (
    .a_0(a_8), .b_0(b_8), .a_1(a_9), .b_1(b_9), .sel(sel), .a_2(a_10), .b_2(b_10), .a_3(a_11), .b_3(b_11),
    .out_10(out_8), .out_11(out_9), .out_12(out_10), .out_13(out_11));
  mux4 mux4_4 (
    .a_0(a_12), .b_0(b_12), .a_1(a_13), .b_1(b_13), .sel(sel), .a_2(a_14), .b_2(b_14), .a_3(a_15),
    .b_3(b_15), .out_10(out_12), .out_11(out_13), .out_12(out_14), .out_13(out_15));
endmodule

module not16 (
  input  in_1,
  input  in_2,
  input  in_3,
  input  in_4,
  input  in_5,
  input  in_6,
  input  in_7,
  input  in_8,
  input  in_9,
  input  in_10,
  input  in_11,
  input  in_12,
  input  in_13,
  input  in_14,
  input  in_15,
  input  in_16,
  output out_17,
  output out_18,
  output out_19,
  output out_20,
  output out_21,
  output out_22,
  output out_23,
  output out_24,
  output out_25,
  output out_26,
  output out_27,
  output out_28,
  output out_29,
  output out_30,
  output out_31,
  output out_32
);

  not not_1 (out_17, in_1);
  not not_2 (out_18, in_2);
  not not_3 (out_19, in_3);
  not not_4 (out_20, in_4);
  not not_5 (out_21, in_5);
  not not_6 (out_22, in_6);
  not not_7 (out_23, in_7);
  not not_8 (out_24, in_8);
  not not_9 (out_25, in_9);
  not not_10 (out_26, in_10);
  not not_11 (out_27, in_11);
  not not_12 (out_28, in_12);
  not not_13 (out_29, in_13);
  not not_14 (out_30, in_14);
  not not_15 (out_31, in_15);
  not not_16 (out_32, in_16);
endmodule

module zn (
  input  in_0,
  input  in_1,
  input  in_2,
  input  in_3,
  input  in_4,
  input  in_5,
  input  in_6,
  input  in_7,
  input  z,
  input  n,
  input  in_8,
  input  in_9,
  input  in_10,
  input  in_11,
  input  in_12,
  input  in_13,
  input  in_14,
  input  in_15,
  output out_19,
  output out_20,
  output out_21,
  output out_22,
  output out_23,
  output out_24,
  output out_25,
  output out_26,
  output out_27,
  output out_28,
  output out_29,
  output out_30,
  output out_31,
  output out_32,
  output out_33,
  output out_34
);

  wire mux16_1_out_0, mux16_1_out_1, mux16_1_out_2, mux16_1_out_3, mux16_1_out_4, mux16_1_out_5,
       mux16_1_out_6, mux16_1_out_7, mux16_1_out_8, mux16_1_out_9, mux16_1_out_10, mux16_1_out_11,
       mux16_1_out_12, mux16_1_out_13, mux16_1_out_14, mux16_1_out_15, not16_1_out_17, not16_1_out_18,
       not16_1_out_19, not16_1_out_20, not16_1_out_21, not16_1_out_22, not16_1_out_23, not16_1_out_24,
       not16_1_out_25, not16_1_out_26, not16_1_out_27, not16_1_out_28, not16_1_out_29, not16_1_out_30,
       not16_1_out_31, not16_1_out_32;

  mux16 mux16_1 (
    .out_0(mux16_1_out_0), .out_1(mux16_1_out_1), .out_2(mux16_1_out_2), .out_3(mux16_1_out_3),
    .out_4(mux16_1_out_4), .out_5(mux16_1_out_5), .out_6(mux16_1_out_6), .out_7(mux16_1_out_7),
    .out_8(mux16_1_out_8), .out_9(mux16_1_out_9), .out_10(mux16_1_out_10), .out_11(mux16_1_out_11),
    .out_12(mux16_1_out_12), .out_13(mux16_1_out_13), .out_14(mux16_1_out_14), .out_15(mux16_1_out_15),
    .a_0(in_0), .b_0(1'b0), .a_1(in_1), .b_1(1'b0), .a_2(in_2), .b_2(1'b0), .a_3(in_3), .b_3(1'b0),
    .a_4(in_4), .b_4(1'b0), .a_5(in_5), .b_5(1'b0), .a_6(in_6), .b_6(1'b0), .a_7(in_7), .b_7(1'b0), .sel(z),
    .a_8(in_8), .b_8(1'b0), .a_9(in_9), .b_9(1'b0), .a_10(in_10), .b_10(1'b0), .a_11(in_11), .b_11(1'b0),
    .a_12(in_12), .b_12(1'b0), .a_13(in_13), .b_13(1'b0), .a_14(in_14), .b_14(1'b0), .a_15(in_15), .b_15(1'b0));
  not16 not16_1 (
    .in_1(mux16_1_out_0), .in_2(mux16_1_out_1), .in_3(mux16_1_out_2), .in_4(mux16_1_out_3),
    .in_5(mux16_1_out_4), .in_6(mux16_1_out_5), .in_7(mux16_1_out_6), .in_8(mux16_1_out_7),
    .in_9(mux16_1_out_8), .in_10(mux16_1_out_9), .in_11(mux16_1_out_10), .in_12(mux16_1_out_11),
    .in_13(mux16_1_out_12), .in_14(mux16_1_out_13), .in_15(mux16_1_out_14), .in_16(mux16_1_out_15),
    .out_17(not16_1_out_17), .out_18(not16_1_out_18), .out_19(not16_1_out_19), .out_20(not16_1_out_20),
    .out_21(not16_1_out_21), .out_22(not16_1_out_22), .out_23(not16_1_out_23), .out_24(not16_1_out_24),
    .out_25(not16_1_out_25), .out_26(not16_1_out_26), .out_27(not16_1_out_27), .out_28(not16_1_out_28),
    .out_29(not16_1_out_29), .out_30(not16_1_out_30), .out_31(not16_1_out_31), .out_32(not16_1_out_32));
  mux16 mux16_2 (
    .out_0(out_19), .out_1(out_20), .out_2(out_21), .out_3(out_22), .out_4(out_23), .out_5(out_24),
    .out_6(out_25), .out_7(out_26), .out_8(out_27), .out_9(out_28), .out_10(out_29), .out_11(out_30),
    .out_12(out_31), .out_13(out_32), .out_14(out_33), .out_15(out_34), .a_0(mux16_1_out_0),
    .b_0(not16_1_out_17), .a_1(mux16_1_out_1), .b_1(not16_1_out_18), .a_2(mux16_1_out_2),
    .b_2(not16_1_out_19), .a_3(mux16_1_out_3), .b_3(not16_1_out_20), .a_4(mux16_1_out_4),
    .b_4(not16_1_out_21), .a_5(mux16_1_out_5), .b_5(not16_1_out_22), .a_6(mux16_1_out_6),
    .b_6(not16_1_out_23), .a_7(mux16_1_out_7), .b_7(not16_1_out_24), .sel(n), .a_8(mux16_1_out_8),
    .b_8(not16_1_out_25), .a_9(mux16_1_out_9), .b_9(not16_1_out_26), .a_10(mux16_1_out_10),
    .b_10(not16_1_out_27), .a_11(mux16_1_out_11), .b_11(not16_1_out_28), .a_12(mux16_1_out_12),
    .b_12(not16_1_out_29), .a_13(mux16_1_out_13), .b_13(not16_1_out_30), .a_14(mux16_1_out_14),
    .b_14(not16_1_out_31), .a_15(mux16_1_out_15), .b_15(not16_1_out_32));
endmodule

module add16 (
  input  a_0,
  input  b_0,
  input  a_1,
  input  b_1,
  input  a_2,
  input  b_2,
  input  a_3,
  input  b_3,
  input  a_4,
  input  b_4,
  input  a_5,
  input  b_5,
  input  a_6,
  input  b_6,
  input  a_7,
  input  b_7,
  input  a_8,
  input  b_8,
  input  a_9,
  input  b_9,
  input  a_10,
  input  b_10,
  input  a_11,
  input  b_11,
  input  a_12,
  input  b_12,
  input  a_13,
  input  b_13,
  input  a_14,
  input  b_14,
  input  a_15,
  input  b_16,
  output out_0,
  output out_1,
  output out_2,
  output out_3,
  output out_4,
  output out_5,
  output out_6,
  output out_7,
  output out_8,
  output out_9,
  output out_10,
  output out_11,
  output out_12,
  output out_13,
  output out_14,
  output out_15,
  output out_49
);

  wire fulladder_1_carry, fulladder_2_carry, fulladder_3_carry, fulladder_4_carry, fulladder_5_carry,
       fulladder_6_carry, fulladder_7_carry, fulladder_8_carry, fulladder_9_carry, fulladder_10_carry,
       fulladder_11_carry, fulladder_12_carry, fulladder_13_carry, fulladder_14_carry, halfadder_1_carry;

  halfadder halfadder_1 (.a(a_0), .b(b_0), .sum(out_0), .carry(halfadder_1_carry));
  fulladder fulladder_1 (.a(a_1), .b(b_1), .c(halfadder_1_carry), .sum(out_1), .carry(fulladder_1_carry));
  fulladder fulladder_2 (.a(a_2), .b(b_2), .c(fulladder_1_carry), .sum(out_2), .carry(fulladder_2_carry));
  fulladder fulladder_3 (.a(a_3), .b(b_3), .c(fulladder_2_carry), .sum(out_3), .carry(fulladder_3_carry));
  fulladder fulladder_4 (.a(a_4), .b(b_4), .c(fulladder_3_carry), .sum(out_4), .carry(fulladder_4_carry));
  fulladder fulladder_5 (.a(a_5), .b(b_5), .c(fulladder_4_carry), .sum(out_5), .carry(fulladder_5_carry));
  fulladder fulladder_6 (.a(a_6), .b(b_6), .c(fulladder_5_carry), .sum(out_6), .carry(fulladder_6_carry));
  fulladder fulladder_7 (.a(a_7), .b(b_7), .c(fulladder_6_carry), .sum(out_7), .carry(fulladder_7_carry));
  fulladder fulladder_8 (.a(a_8), .b(b_8), .c(fulladder_7_carry), .sum(out_8), .carry(fulladder_8_carry));
  fulladder fulladder_9 (.a(a_9), .b(b_9), .c(fulladder_8_carry), .sum(out_9), .carry(fulladder_9_carry));
  fulladder fulladder_10 (.a(a_10), .b(b_10), .c(fulladder_9_carry), .sum(out_10), .carry(fulladder_10_carry));
  fulladder fulladder_11 (.a(a_11), .b(b_11), .c(fulladder_10_carry), .sum(out_11), .carry(fulladder_11_carry));
  fulladder fulladder_12 (.a(a_12), .b(b_12), .c(fulladder_11_carry), .sum(out_12), .carry(fulladder_12_carry));
  fulladder fulladder_13 (.a(a_13), .b(b_13), .c(fulladder_12_carry), .sum(out_13), .carry(fulladder_13_carry));
  fulladder fulladder_14 (.a(a_14), .b(b_14), .c(fulladder_13_carry), .sum(out_14), .carry(fulladder_14_carry));
  fulladder fulladder_15 (.a(a_15), .b(b_16), .c(fulladder_14_carry), .sum(out_15), .carry(out_49));
endmodule

module halfadder (
  input  a,
  input  b,
  output sum,
  output carry
);

  and and_1 (carry, a, b);
  xor xor_1 (sum, a, b);
endmodule

module fulladder (
  input  a,
  input  b,
  input  c,
  output sum,
  output carry
);

  wire halfadder_1_carry, halfadder_1_sum, halfadder_2_carry;

  halfadder halfadder_1 (.a(a), .b(b), .sum(halfadder_1_sum), .carry(halfadder_1_carry));
  halfadder halfadder_2 (.a(c), .b(halfadder_1_sum), .sum(sum), .carry(halfadder_2_carry));
  or or_1 (carry, halfadder_1_carry, halfadder_2_carry);
endmodule

module add162 (
  input  a_0,
  input  a_1,
  input  a_2,
  input  a_3,
  input  a_4,
  input  a_5,
  input  a_6,
  input  a_7,
  input  a_8,
  input  a_9,
  input  a_10,
  input  a_11,
  input  a_12,
  input  a_13,
  input  a_14,
  input  a_15,
  input  b_0,
  input  b_1,
  input  b_2,
  input  b_3,
  input  b_4,
  input  b_5,
  input  b_6,
  input  b_7,
  input  b_8,
  input  b_9,
  input  b_10,
  input  b_11,
  input  b_12,
  input  b_13,
  input  b_14,
  input  b_15,
  output out_0,
  output out_1,
  output out_2,
  output out_3,
  output out_4,
  output out_5,
  output out_6,
  output out_7,
  output out_8,
  output out_9,
  output out_10,
  output out_11,
  output out_12,
  output out_13,
  output out_14,
  output out_15,
  output carry
);

  wire fulladder_1_carry, fulladder_2_carry, fulladder_3_carry, fulladder_4_carry, fulladder_5_carry,
       fulladder_6_carry, fulladder_7_carry, fulladder_8_carry, fulladder_9_carry, fulladder_10_carry,
       fulladder_11_carry, fulladder_12_carry, fulladder_13_carry, fulladder_14_carry, halfadder_1_carry;

  halfadder halfadder_1 (.a(a_0), .b(b_0), .sum(out_0), .carry(halfadder_1_carry));
  fulladder fulladder_1 (.a(a_1), .b(b_1), .c(halfadder_1_carry), .sum(out_1), .carry(fulladder_1_carry));
  fulladder fulladder_2 (.a(a_2), .b(b_2), .c(fulladder_1_carry), .sum(out_2), .carry(fulladder_2_carry));
  fulladder fulladder_3 (.a(a_3), .b(b_3), .c(fulladder_2_carry), .sum(out_3), .carry(fulladder_3_carry));
  fulladder fulladder_4 (.a(a_4), .b(b_4), .c(fulladder_3_carry), .sum(out_4), .carry(fulladder_4_carry));
  fulladder fulladder_5 (.a(a_5), .b(b_5), .c(fulladder_4_carry), .sum(out_5), .carry(fulladder_5_carry));
  fulladder fulladder_6 (.a(a_6), .b(b_6), .c(fulladder_5_carry), .sum(out_6), .carry(fulladder_6_carry));
  fulladder fulladder_7 (.a(a_7), .b(b_7), .c(fulladder_6_carry), .sum(out_7), .carry(fulladder_7_carry));
  fulladder fulladder_8 (.a(a_8), .b(b_8), .c(fulladder_7_carry), .sum(out_8), .carry(fulladder_8_carry));
  fulladder fulladder_9 (.a(a_9), .b(b_9), .c(fulladder_8_carry), .sum(out_9), .carry(fulladder_9_carry));
  fulladder fulladder_10 (.a(a_10), .b(b_10), .c(fulladder_9_carry), .sum(out_10), .carry(fulladder_10_carry));
  fulladder fulladder_11 (.a(a_11), .b(b_11), .c(fulladder_10_carry), .sum(out_11), .carry(fulladder_11_carry));
  fulladder fulladder_12 (.a(a_12), .b(b_12), .c(fulladder_11_carry), .sum(out_12), .carry(fulladder_12_carry));
  fulladder fulladder_13 (.a(a_13), .b(b_13), .c(fulladder_12_carry), .sum(out_13), .carry(fulladder_13_carry));
  fulladder fulladder_14 (.a(a_14), .b(b_14), .c(fulladder_13_carry), .sum(out_14), .carry(fulladder_14_carry));
  fulladder fulladder_15 (.a(a_15), .b(b_15), .c(fulladder_14_carry), .sum(out_15), .carry(carry));
endmodule

module and16 (
  input  a_0,
  input  a_1,
  input  a_2,
  input  a_3,
  input  a_4,
  input  a_5,
  input  a_6,
  input  a_7,
  input  a_8,
  input  a_9,
  input  a_10,
  input  a_11,
  input  a_12,
  input  a_13,
  input  a_14,
  input  a_15,
  input  b_0,
  input  b_1,
  input  b_2,
  input  b_3,
  input  b_4,
  input  b_5,
  input  b_6,
  input  b_7,
  input  b_8,
  input  b_9,
  input  b_10,
  input  b_11,
  input  b_12,
  input  b_13,
  input  b_14,
  input  b_15,
  output out_0,
  output out_1,
  output out_2,
  output out_3,
  output out_4,
  output out_5,
  output out_6,
  output out_7,
  output out_8,
  output out_9,
  output out_10,
  output out_11,
  output out_12,
  output out_13,
  output out_14,
  output out_15
);

  and and_1 (out_0, a_0, b_0);
  and and_2 (out_1, a_1, b_1);
  and and_3 (out_2, a_2, b_2);
  and and_4 (out_3, a_3, b_3);
  and and_5 (out_4, a_4, b_4);
  and and_6 (out_5, a_5, b_5);
  and and_7 (out_6, a_6, b_6);
  and and_8 (out_7, a_7, b_7);
  and and_9 (out_8, a_8, b_8);
  and and_10 (out_9, a_9, b_9);
  and and_11 (out_10, a_10, b_10);
  and and_12 (out_11, a_11, b_11);
  and and_13 (out_12, a_12, b_12);
  and and_14 (out_13, a_13, b_13);
  and and_15 (out_14, a_14, b_14);
  and and_16 (out_15, a_15, b_15);
endmodule

module alu1 (
  input  x_0,
  input  x_1,
  input  x_2,
  input  x_3,
  input  x_4,
  input  x_5,
  input  x_6,
  input  x_7,
  input  zx,
  input  nx,
  input  x_8,
  input  x_9,
  input  x_10,
  input  x_11,
  input  x_12,
  input  x_13,
  input  x_14,
  input  x_15,
  input  f,
  input  no,
  input  y_0,
  input  y_1,
  input  y_2,
  input  y_3,
  input  y_4,
  input  y_5,
  input  y_6,
  input  y_7,
  input  zy,
  input  ny,
  input  y_8,
  input  y_9,
  input  y_10,
  input  y_11,
  input  y_12,
  input  y_13,
  input  y_14,
  input  y_15,
  output out_0,
  output out_1,
  output out_2,
  output out_3,
  output out_4,
  output out_5,
  output out_6,
  output out_7,
  output out_8,
  output out_9,
  output out_10,
  output out_11,
  output out_12,
  output out_13,
  output out_14,
  output out_15
);

  wire add162_1_out_0, add162_1_out_1, add162_1_out_2, add162_1_out_3, add162_1_out_4, add162_1_out_5,
       add162_1_out_6, add162_1_out_7, add162_1_out_8, add162_1_out_9, add162_1_out_10, add162_1_out_11,
       add162_1_out_12, add162_1_out_13, add162_1_out_14, add162_1_out_15, and16_1_out_0, and16_1_out_1,
       and16_1_out_2, and16_1_out_3, and16_1_out_4, and16_1_out_5, and16_1_out_6, and16_1_out_7,
       and16_1_out_8, and16_1_out_9, and16_1_out_10, and16_1_out_11, and16_1_out_12, and16_1_out_13,
       and16_1_out_14, and16_1_out_15, mux16_1_out_0, mux16_1_out_1, mux16_1_out_2, mux16_1_out_3,
       mux16_1_out_4, mux16_1_out_5, mux16_1_out_6, mux16_1_out_7, mux16_1_out_8, mux16_1_out_9,
       mux16_1_out_10, mux16_1_out_11, mux16_1_out_12, mux16_1_out_13, mux16_1_out_14, mux16_1_out_15,
       not16_1_out_17, not16_1_out_18, not16_1_out_19, not16_1_out_20, not16_1_out_21, not16_1_out_22,
       not16_1_out_23, not16_1_out_24, not16_1_out_25, not16_1_out_26, not16_1_out_27, not16_1_out_28,
       not16_1_out_29, not16_1_out_30, not16_1_out_31, not16_1_out_32, zn_1_out_19, zn_1_out_20, zn_1_out_21,
       zn_1_out_22, zn_1_out_23, zn_1_out_24, zn_1_out_25, zn_1_out_26, zn_1_out_27, zn_1_out_28,
       zn_1_out_29, zn_1_out_30, zn_1_out_31, zn_1_out_32, zn_1_out_33, zn_1_out_34, zn_2_out_19,
       zn_2_out_20, zn_2_out_21, zn_2_out_22, zn_2_out_23, zn_2_out_24, zn_2_out_25, zn_2_out_26,
       zn_2_out_27, zn_2_out_28, zn_2_out_29, zn_2_out_30, zn_2_out_31, zn_2_out_32, zn_2_out_33, zn_2_out_34;

  zn zn_1 (
    .in_0(x_0), .in_1(x_1), .in_2(x_2), .in_3(x_3), .in_4(x_4), .in_5(x_5), .in_6(x_6), .in_7(x_7), .z(zx),
    .n(nx), .in_8(x_8), .in_9(x_9), .in_10(x_10), .in_11(x_11), .in_12(x_12), .in_13(x_13), .in_14(x_14),
    .in_15(x_15), .out_19(zn_1_out_19), .out_20(zn_1_out_20), .out_21(zn_1_out_21), .out_22(zn_1_out_22),
    .out_23(zn_1_out_23), .out_24(zn_1_out_24), .out_25(zn_1_out_25), .out_26(zn_1_out_26),
    .out_27(zn_1_out_27), .out_28(zn_1_out_28), .out_29(zn_1_out_29), .out_30(zn_1_out_30),
    .out_31(zn_1_out_31), .out_32(zn_1_out_32), .out_33(zn_1_out_33), .out_34(zn_1_out_34));
  zn zn_2 (
    .in_0(y_0), .in_1(y_1), .in_2(y_2), .in_3(y_3), .in_4(y_4), .in_5(y_5), .in_6(y_6), .in_7(y_7), .z(zy),
    .n(ny), .in_8(y_8), .in_9(y_9), .in_10(y_10), .in_11(y_11), .in_12(y_12), .in_13(y_13), .in_14(y_14),
    .in_15(y_15), .out_19(zn_2_out_19), .out_20(zn_2_out_20), .out_21(zn_2_out_21), .out_22(zn_2_out_22),
    .out_23(zn_2_out_23), .out_24(zn_2_out_24), .out_25(zn_2_out_25), .out_26(zn_2_out_26),
    .out_27(zn_2_out_27), .out_28(zn_2_out_28), .out_29(zn_2_out_29), .out_30(zn_2_out_30),
    .out_31(zn_2_out_31), .out_32(zn_2_out_32), .out_33(zn_2_out_33), .out_34(zn_2_out_34));
  add162 add162_1 (
    .a_0(zn_1_out_19), .a_1(zn_1_out_20), .a_2(zn_1_out_21), .a_3(zn_1_out_22), .a_4(zn_1_out_23),
    .a_5(zn_1_out_24), .a_6(zn_1_out_25), .a_7(zn_1_out_26), .a_8(zn_1_out_27), .a_9(zn_1_out_28),
    .a_10(zn_1_out_29), .a_11(zn_1_out_30), .a_12(zn_1_out_31), .a_13(zn_1_out_32), .a_14(zn_1_out_33),
    .a_15(zn_1_out_34), .b_0(zn_2_out_19), .b_1(zn_2_out_20), .b_2(zn_2_out_21), .b_3(zn_2_out_22),
    .b_4(zn_2_out_23), .b_5(zn_2_out_24), .b_6(zn_2_out_25), .b_7(zn_2_out_26), .b_8(zn_2_out_27),
    .b_9(zn_2_out_28), .b_10(zn_2_out_29), .b_11(zn_2_out_30), .b_12(zn_2_out_31), .b_13(zn_2_out_32),
    .b_14(zn_2_out_33), .b_15(zn_2_out_34), .out_0(add162_1_out_0), .out_1(add162_1_out_1),
    .out_2(add162_1_out_2), .out_3(add162_1_out_3), .out_4(add162_1_out_4), .out_5(add162_1_out_5),
    .out_6(add162_1_out_6), .out_7(add162_1_out_7), .out_8(add162_1_out_8), .out_9(add162_1_out_9),
    .out_10(add162_1_out_10), .out_11(add162_1_out_11), .out_12(add162_1_out_12), .out_13(add162_1_out_13),
    .out_14(add162_1_out_14), .out_15(add162_1_out_15));  // open: carry
  and16 and16_1 (
    .a_0(zn_1_out_19), .a_1(zn_1_out_20), .a_2(zn_1_out_21), .a_3(zn_1_out_22), .a_4(zn_1_out_23),
    .a_5(zn_1_out_24), .a_6(zn_1_out_25), .a_7(zn_1_out_26), .a_8(zn_1_out_27), .a_9(zn_1_out_28),
    .a_10(zn_1_out_29), .a_11(zn_1_out_30), .a_12(zn_1_out_31), .a_13(zn_1_out_32), .a_14(zn_1_out_33),
    .a_15(zn_1_out_34), .b_0(zn_2_out_19), .b_1(zn_2_out_20), .b_2(zn_2_out_21), .b_3(zn_2_out_22),
    .b_4(zn_2_out_23), .b_5(zn_2_out_24), .b_6(zn_2_out_25), .b_7(zn_2_out_26), .b_8(zn_2_out_27),
    .b_9(zn_2_out_28), .b_10(zn_2_out_29), .b_11(zn_2_out_30), .b_12(zn_2_out_31), .b_13(zn_2_out_32),
    .b_14(zn_2_out_33), .b_15(zn_2_out_34), .out_0(and16_1_out_0), .out_1(and16_1_out_1),
    .out_2(and16_1_out_2), .out_3(and16_1_out_3), .out_4(and16_1_out_4), .out_5(and16_1_out_5),
    .out_6(and16_1_out_6), .out_7(and16_1_out_7), .out_8(and16_1_out_8), .out_9(and16_1_out_9),
    .out_10(and16_1_out_10), .out_11(and16_1_out_11), .out_12(and16_1_out_12), .out_13(and16_1_out_13),
    .out_14(and16_1_out_14), .out_15(and16_1_out_15));
  mux16 mux16_1 (
    .out_0(mux16_1_out_0), .out_1(mux16_1_out_1), .out_2(mux16_1_out_2), .out_3(mux16_1_out_3),
    .out_4(mux16_1_out_4), .out_5(mux16_1_out_5), .out_6(mux16_1_out_6), .out_7(mux16_1_out_7),
    .out_8(mux16_1_out_8), .out_9(mux16_1_out_9), .out_10(mux16_1_out_10), .out_11(mux16_1_out_11),
    .out_12(mux16_1_out_12), .out_13(mux16_1_out_13), .out_14(mux16_1_out_14), .out_15(mux16_1_out_15),
    .a_0(and16_1_out_0), .b_0(add162_1_out_0), .a_1(and16_1_out_1), .b_1(add162_1_out_1),
    .a_2(and16_1_out_2), .b_2(add162_1_out_2), .a_3(and16_1_out_3), .b_3(add162_1_out_3),
    .a_4(and16_1_out_4), .b_4(add162_1_out_4), .a_5(and16_1_out_5), .b_5(add162_1_out_5),
    .a_6(and16_1_out_6), .b_6(add162_1_out_6), .a_7(and16_1_out_7), .b_7(add162_1_out_7), .sel(f),
    .a_8(and16_1_out_8), .b_8(add162_1_out_8), .a_9(and16_1_out_9), .b_9(add162_1_out_9),
    .a_10(and16_1_out_10), .b_10(add162_1_out_10), .a_11(and16_1_out_11), .b_11(add162_1_out_11),
    .a_12(and16_1_out_12), .b_12(add162_1_out_12), .a_13(and16_1_out_13), .b_13(add162_1_out_13),
    .a_14(and16_1_out_14), .b_14(add162_1_out_14), .a_15(and16_1_out_15), .b_15(add162_1_out_15));
  not16 not16_1 (
    .in_1(mux16_1_out_0), .in_2(mux16_1_out_1), .in_3(mux16_1_out_2), .in_4(mux16_1_out_3),
    .in_5(mux16_1_out_4), .in_6(mux16_1_out_5), .in_7(mux16_1_out_6), .in_8(mux16_1_out_7),
    .in_9(mux16_1_out_8), .in_10(mux16_1_out_9), .in_11(mux16_1_out_10), .in_12(mux16_1_out_11),
    .in_13(mux16_1_out_12), .in_14(mux16_1_out_13), .in_15(mux16_1_out_14), .in_16(mux16_1_out_15),
    .out_17(not16_1_out_17), .out_18(not16_1_out_18), .out_19(not16_1_out_19), .out_20(not16_1_out_20),
    .out_21(not16_1_out_21), .out_22(not16_1_out_22), .out_23(not16_1_out_23), .out_24(not16_1_out_24),
    .out_25(not16_1_out_25), .out_26(not16_1_out_26), .out_27(not16_1_out_27), .out_28(not16_1_out_28),
    .out_29(not16_1_out_29), .out_30(not16_1_out_30), .out_31(not16_1_out_31), .out_32(not16_1_out_32));
  mux16 mux16_2 (
    .out_0(out_0), .out_1(out_1), .out_2(out_2), .out_3(out_3), .out_4(out_4), .out_5(out_5), .out_6(out_6),
    .out_7(out_7), .out_8(out_8), .out_9(out_9), .out_10(out_10), .out_11(out_11), .out_12(out_12),
    .out_13(out_13), .out_14(out_14), .out_15(out_15), .a_0(mux16_1_out_0), .b_0(not16_1_out_17),
    .a_1(mux16_1_out_1), .b_1(not16_1_out_18), .a_2(mux16_1_out_2), .b_2(not16_1_out_19),
    .a_3(mux16_1_out_3), .b_3(not16_1_out_20), .a_4(mux16_1_out_4), .b_4(not16_1_out_21),
    .a_5(mux16_1_out_5), .b_5(not16_1_out_22), .a_6(mux16_1_out_6), .b_6(not16_1_out_23),
    .a_7(mux16_1_out_7), .b_7(not16_1_out_24), .sel(no), .a_8(mux16_1_out_8), .b_8(not16_1_out_25),
    .a_9(mux16_1_out_9), .b_9(not16_1_out_26), .a_10(mux16_1_out_10), .b_10(not16_1_out_27),
    .a_11(mux16_1_out_11), .b_11(not16_1_out_28), .a_12(mux16_1_out_12), .b_12(not16_1_out_29),
    .a_13(mux16_1_out_13), .b_13(not16_1_out_30), .a_14(mux16_1_out_14), .b_14(not16_1_out_31),
    .a_15(mux16_1_out_15), .b_15(not16_1_out_32));
endmodule

module or8way (
  input  in_0,
  input  in_1,
  input  in_2,
  input  in_3,
  input  in_4,
  input  in_5,
  input  in_6,
  input  in_7,
  output out
);

  wire or_1_out, or_2_out, or_3_out, or_4_out, or_5_out, or_6_out;

  or or_1 (or_1_out, in_0, in_1);
  or or_2 (or_2_out, in_2, in_3);
  or or_3 (or_3_out, in_4, in_5);
  or or_4 (or_4_out, in_6, in_7);
  or or_5 (or_5_out, or_1_out, or_2_out);
  or or_6 (or_6_out, or_3_out, or_4_out);
  or or_7 (out, or_5_out, or_6_out);
endmodule
