// Logisim project inc.circ as structural Verilog: 1 circuit, main circuit main
module main (
  input  in_1,
  input  in_2,
  input  in_3,
  input  in_4,
  input  in_5,
  output out_6,
  output out_7,
  output out_8,
  output out_9,
  output out_10
);

  wire and_1_out, and_2_out, and_3_out;

  xor xor_1 (out_6, in_1, in_2);
  and and_1 (and_1_out, in_1, in_2);
  xor xor_2 (out_7, and_1_out, in_3);
  and and_2 (and_2_out, and_1_out, in_3);
  xor xor_3 (out_8, and_2_out, in_4);
  and and_3 (and_3_out, and_2_out, in_4);
  xor xor_4 (out_9, and_3_out, in_5);
  and and_4 (out_10, and_3_out, in_5);
endmodule
