// Logisim project latches.circ as structural Verilog: 1 circuit, main circuit main
module main (
  input  in_1,
  input  in_2,
  input  in_3,
  input  in_4,
  output out_5,
  output out_6,
  output out_7,
  output out_8
);

  wire and_1_out, and_2_out, not_1_out;

  nor nor_1 (out_6, in_1, out_8);
  nor nor_2 (out_8, out_6, in_3);
  not not_1 (not_1_out, in_4);
  and and_1 (and_1_out, not_1_out, in_2);
  and and_2 (and_2_out, in_2, in_4);
  nor nor_3 (out_5, and_1_out, out_7);
  nor nor_4 (out_7, out_5, and_2_out);
endmodule
