// Logisim project mux16.circ as structural Verilog: 5 circuits, main circuit main
module main (
  input  in_1,
  input  in_2,
  input  in_3,
  input  in_4,
  input  in_5,
  input  in_6,
  input  in_7,
  input  in_8,
  input  in_9,
  input  in_10,
  input  in_11,
  input  in_12,
  output out_13,
  output out_14,
  output out_15,
  output out_16,
  output out_17
);

  mux mux_1 (.a(in_1), .b(in_2), .sel(in_3), .out_4(out_13));
  mux4 mux4_1 (
    .a_0(in_4), .b_0(in_5), .a_1(in_6), .b_1(in_7), .sel(in_8), .a_2(in_9), .b_2(in_10), .a_3(in_11),
    .b_3(in_12), .out_10(out_14), .out_11(out_15), .out_12(out_16), .out_13(out_17));
  mux16_2 mux16_1 ();  // open: out_0, out_1, out_2, out_3, out_4, out_5, out_6, out_7, out_8, out_9, out_10, out_11, out_12, out_13, out_14, out_15, a_0, b_0, a_1, b_1, a_2, b_2, a_3, b_3, a_4, b_4, a_5, b_5, a_6, b_6, a_7, b_7, sel, a_8, b_8, a_9, b_9, a_10, b_10, a_11, b_11, a_12, b_12, a_13, b_13, a_14, b_14, a_15, b_15
endmodule

module mux (
  input  a,
  input  b,
  input  sel,
  output out_4
);

  wire and_1_out, and_2_out, not_1_out;

  not not_1 (not_1_out, sel);
  and and_1 (and_1_out, a, not_1_out);
  and and_2 (and_2_out, b, sel);
  or or_1 (out_4, and_1_out, and_2_out);
endmodule

module mux4 (
  input  a_0,
  input  b_0,
  input  a_1,
  input  b_1,
  input  sel,
  input  a_2,
  input  b_2,
  input  a_3,
  input  b_3,
  output out_10,
  output out_11,
  output out_12,
  output out_13
);

  mux mux_1 (.a(a_0), .b(b_0), .sel(sel), .out_4(out_10));
  mux mux_2 (.a(a_1), .b(b_1), .sel(sel), .out_4(out_11));
  mux mux_3 (.a(a_2), .b(b_2), .sel(sel), .out_4(out_12));
  mux mux_4 (.a(a_3), .b(b_3), .sel(sel), .out_4(out_13));
endmodule

module mux16 (
  input  a_0,
  input  b_0,
  input  a_1,
  input  b_1,
  input  a_2,
  input  b_2,
  input  a_4,
  input  a_3,
  input  b_4,
  input  b_3,
  input  a_5,
  input  b_5,
  input  a_6,
  input  b_6,
  input  a_8,
  input  a_7,
  input  b_8,
  input  b_7,
  input  a_9,
  input  b_9,
  input  sel,
  input  a_10,
  input  a_12,
  input  b_10,
  input  b_12,
  input  a_11,
  input  a_13,
  input  b_11,
  input  b_13,
  input  a_14,
  input  b_14,
  input  a_15,
  input  b_15,
  output out_0,
  output out_1,
  output out_2,
  output out_3,
  output out_4,
  output out_5,
  output out_6,
  output out_7,
  output out_8,
  output out_9,
  output out_10,
  output out_11,
  output out_12,
  output out_13,
  output out_14,
  output out_15
);

  mux4 mux4_1 (
    .a_0(a_0), .b_0(b_0), .a_1(a_1), .b_1(b_1), .sel(sel), .a_2(a_2), .b_2(b_2), .a_3(a_3), .b_3(b_3),
    .out_10(out_0), .out_11(out_1), .out_12(out_2), .out_13(out_3));
  mux4 mux4_2 (
    .a_0(a_4), .b_0(b_4), .a_1(a_5), .b_1(b_5), .sel(sel), .a_2(a_6), .b_2(b_6), .a_3(a_7), .b_3(b_7),
    .out_10(out_4), .out_11(out_5), .out_12(out_6), .out_13(out_7));
  mux4 mux4_3 (
    .a_0(a_8), .b_0(b_8), .a_1(a_9), .b_1(b_9), .sel(sel), .a_2(a_10), .b_2(b_10), .a_3(a_11), .b_3(b_11),
    .out_10(out_8), .out_11(out_9), .out_12(out_10), .out_13(out_11));
  mux4 mux4_4 (
    .a_0(a_12), .b_0(b_12), .a_1(a_13), .b_1(b_13), .sel(sel), .a_2(a_14), .b_2(b_14), .a_3(a_15),
    .b_3(b_15), .out_10(out_12), .out_11(out_13), .out_12(out_14), .out_13(out_15));
endmodule

module mux16_2 (
  input  a_0,
  input  b_0,
  input  a_1,
  input  b_1,
  input  a_2,
  input  b_2,
  input  a_3,
  input  b_3,
  input  a_4,
  input  b_4,
  input  a_5,
  input  b_5,
  input  a_6,
  input  b_6,
  input  a_7,
  input  b_7,
  input  a_8,
  input  b_8,
  input  a_9,
  input  b_9,
  input  a_10,
  input  b_10,
  input  a_11,
  input  b_11,
  input  a_12,
  input  b_12,
  input  a_13,
  input  b_13,
  input  a_14,
  input  b_14,
  input  a_15,
  input  b_15,
  input  sel,
  output out_0,
  output out_1,
  output out_2,
  output out_3,
  output out_4,
  output out_5,
  output out_6,
  output out_7,
  output out_8,
  output out_9,
  output out_10,
  output out_11,
  output out_12,
  output out_13,
  output out_14,
  output out_15
);

  mux4 mux4_1 (
    .a_0(a_0), .b_0(b_0), .a_1(a_1), .b_1(b_1), .sel(sel), .a_2(a_2), .b_2(b_2), .a_3(a_3), .b_3(b_3),
    .out_10(out_0), .out_11(out_1), .out_12(out_2), .out_13(out_3));
  mux4 mux4_2 (
    .a_0(a_4), .b_0(b_4), .a_1(a_5), .b_1(b_5), .sel(sel), .a_2(a_6), .b_2(b_6), .a_3(a_7), .b_3(b_7),
    .out_10(out_4), .out_11(out_5), .out_12(out_6), .out_13(out_7));
  mux4 mux4_3 (
    .a_0(a_8), .b_0(b_8), .a_1(a_9), .b_1(b_9), .sel(sel), .a_2(a_10), .b_2(b_10), .a_3(a_11), .b_3(b_11),
    .out_10(out_8), .out_11(out_9), .out_12(out_10), .out_13(out_11));
  mux4 mux4_4 (
    .a_0(a_12), .b_0(b_12), .a_1(a_13), .b_1(b_13), .sel(sel), .a_2(a_14), .b_2(b_14), .a_3(a_15),
    .b_3(b_15), .out_10(out_12), .out_11(out_13), .out_12(out_14), .out_13(out_15));
endmodule
