// Logisim project not16.circ as structural Verilog: 2 circuits, main circuit main
module main (
);

  not16 not16_1 ();  // open: in_1, in_2, in_3, in_4, in_5, in_6, in_7, in_8, in_9, in_10, in_11, in_12, in_13, in_14, in_15, in_16, out_17, out_18, out_19, out_20, out_21, out_22, out_23, out_24, out_25, out_26, out_27, out_28, out_29, out_30, out_31, out_32
endmodule

module not16 (
  input  in_1,
  input  in_2,
  input  in_3,
  input  in_4,
  input  in_5,
  input  in_6,
  input  in_7,
  input  in_8,
  input  in_9,
  input  in_10,
  input  in_11,
  input  in_12,
  input  in_13,
  input  in_14,
  input  in_15,
  input  in_16,
  output out_17,
  output out_18,
  output out_19,
  output out_20,
  output out_21,
  output out_22,
  output out_23,
  output out_24,
  output out_25,
  output out_26,
  output out_27,
  output out_28,
  output out_29,
  output out_30,
  output out_31,
  output out_32
);

  not not_1 (out_17, in_1);
  not not_2 (out_18, in_2);
  not not_3 (out_19, in_3);
  not not_4 (out_20, in_4);
  not not_5 (out_21, in_5);
  not not_6 (out_22, in_6);
  not not_7 (out_23, in_7);
  not not_8 (out_24, in_8);
  not not_9 (out_25, in_9);
  not not_10 (out_26, in_10);
  not not_11 (out_27, in_11);
  not not_12 (out_28, in_12);
  not not_13 (out_29, in_13);
  not not_14 (out_30, in_14);
  not not_15 (out_31, in_15);
  not not_16 (out_32, in_16);
endmodule
