// Logisim project pc8.circ as structural Verilog: 10 circuits, main circuit main
module main (
  input  inc,
  input  load,
  input  reset,
  input  in_0,
  input  in_1,
  input  in_2,
  input  in_3,
  input  in_4,
  input  in_5,
  input  in_6,
  input  in_7,
  output out_0,
  output out_1,
  output out_2,
  output out_3,
  output out_4,
  output out_5,
  output out_6,
  output out_7
);

  wire clock_1_out, inc8_1_out_0, inc8_1_out_1, inc8_1_out_2, inc8_1_out_3, inc8_1_out_4, inc8_1_out_5,
       inc8_1_out_6, inc8_1_out_7, mux8_1_out_0, mux8_1_out_1, mux8_1_out_2, mux8_1_out_3, mux8_1_out_4,
       mux8_1_out_5, mux8_1_out_6, mux8_1_out_7, mux8_2_out_0, mux8_2_out_1, mux8_2_out_2, mux8_2_out_3,
       mux8_2_out_4, mux8_2_out_5, mux8_2_out_6, mux8_2_out_7, mux8_3_out_0, mux8_3_out_1, mux8_3_out_2,
       mux8_3_out_3, mux8_3_out_4, mux8_3_out_5, mux8_3_out_6, mux8_3_out_7;

  inc8 inc8_1 (
    .a_0(out_0), .a_1(out_1), .a_2(out_2), .a_3(out_3), .a_4(out_4), .a_5(out_5), .a_6(out_6), .a_7(out_7),
    .out_0(inc8_1_out_0), .out_1(inc8_1_out_1), .out_2(inc8_1_out_2), .out_3(inc8_1_out_3),
    .out_4(inc8_1_out_4), .out_5(inc8_1_out_5), .out_6(inc8_1_out_6), .out_7(inc8_1_out_7));
  mux8 mux8_1 (
    .sel(inc), .a_0(inc8_1_out_0), .b_0(out_0), .a_1(inc8_1_out_1), .b_1(out_1), .a_2(inc8_1_out_2),
    .b_2(out_2), .a_3(inc8_1_out_3), .b_3(out_3), .a_4(inc8_1_out_4), .b_4(out_4), .a_5(inc8_1_out_5),
    .b_5(out_5), .a_6(inc8_1_out_6), .b_6(out_6), .a_7(inc8_1_out_7), .b_7(out_7), .out_0(mux8_1_out_0),
    .out_1(mux8_1_out_1), .out_2(mux8_1_out_2), .out_3(mux8_1_out_3), .out_4(mux8_1_out_4),
    .out_5(mux8_1_out_5), .out_6(mux8_1_out_6), .out_7(mux8_1_out_7));
  mux8 mux8_2 (
    .sel(load), .a_0(mux8_1_out_0), .b_0(in_0), .a_1(mux8_1_out_1), .b_1(in_1), .a_2(mux8_1_out_2),
    .b_2(in_2), .a_3(mux8_1_out_3), .b_3(in_3), .a_4(mux8_1_out_4), .b_4(in_4), .a_5(mux8_1_out_5),
    .b_5(in_5), .a_6(mux8_1_out_6), .b_6(in_6), .a_7(mux8_1_out_7), .b_7(in_7), .out_0(mux8_2_out_0),
    .out_1(mux8_2_out_1), .out_2(mux8_2_out_2), .out_3(mux8_2_out_3), .out_4(mux8_2_out_4),
    .out_5(mux8_2_out_5), .out_6(mux8_2_out_6), .out_7(mux8_2_out_7));
  mux8 mux8_3 (
    .sel(reset), .a_0(mux8_2_out_0), .b_0(1'b0), .a_1(mux8_2_out_1), .b_1(1'b0), .a_2(mux8_2_out_2),
    .b_2(1'b0), .a_3(mux8_2_out_3), .b_3(1'b0), .a_4(mux8_2_out_4), .b_4(1'b0), .a_5(mux8_2_out_5),
    .b_5(1'b0), .a_6(mux8_2_out_6), .b_6(1'b0), .a_7(mux8_2_out_7), .b_7(1'b0), .out_0(mux8_3_out_0),
    .out_1(mux8_3_out_1), .out_2(mux8_3_out_2), .out_3(mux8_3_out_3), .out_4(mux8_3_out_4),
    .out_5(mux8_3_out_5), .out_6(mux8_3_out_6), .out_7(mux8_3_out_7));
  Clock clock_1 (.out(clock_1_out));
  \reg  reg_1 (
    .clock(clock_1_out), .load(1'b1), .in_0(mux8_3_out_0), .in_1(mux8_3_out_1), .in_2(mux8_3_out_2),
    .in_3(mux8_3_out_3), .in_4(mux8_3_out_4), .in_5(mux8_3_out_5), .in_6(mux8_3_out_6), .in_7(mux8_3_out_7),
    .out_0(out_0), .out_1(out_1), .out_2(out_2), .out_3(out_3), .out_4(out_4), .out_5(out_5), .out_6(out_6),
    .out_7(out_7));
endmodule

module halfadder (
  input  a,
  input  b,
  output sum,
  output carry
);

  and and_1 (carry, a, b);
  xor xor_1 (sum, a, b);
endmodule

module fulladder (
  input  a,
  input  b,
  input  c,
  output sum,
  output carry
);

  wire halfadder_1_carry, halfadder_1_sum, halfadder_2_carry;

  halfadder halfadder_1 (.a(a), .b(b), .sum(halfadder_1_sum), .carry(halfadder_1_carry));
  halfadder halfadder_2 (.a(c), .b(halfadder_1_sum), .sum(sum), .carry(halfadder_2_carry));
  or or_1 (carry, halfadder_1_carry, halfadder_2_carry);
endmodule

module add8 (
  input  a_0,
  input  a_1,
  input  a_2,
  input  a_3,
  input  a_4,
  input  a_5,
  input  a_6,
  input  a_7,
  input  b_0,
  input  b_1,
  input  b_2,
  input  b_3,
  input  b_4,
  input  b_5,
  input  b_6,
  input  b_7,
  output out_0,
  output out_1,
  output out_2,
  output out_3,
  output out_4,
  output out_5,
  output out_6,
  output out_7,
  output carry
);

  wire fulladder_1_carry, fulladder_2_carry, fulladder_3_carry, fulladder_4_carry, fulladder_5_carry,
       fulladder_6_carry, halfadder_1_carry;

  halfadder halfadder_1 (.a(a_0), .b(b_0), .sum(out_0), .carry(halfadder_1_carry));
  fulladder fulladder_1 (.a(a_1), .b(b_1), .c(halfadder_1_carry), .sum(out_1), .carry(fulladder_1_carry));
  fulladder fulladder_2 (.a(a_2), .b(b_2), .c(fulladder_1_carry), .sum(out_2), .carry(fulladder_2_carry));
  fulladder fulladder_3 (.a(a_3), .b(b_3), .c(fulladder_2_carry), .sum(out_3), .carry(fulladder_3_carry));
  fulladder fulladder_4 (.a(a_4), .b(b_4), .c(fulladder_3_carry), .sum(out_4), .carry(fulladder_4_carry));
  fulladder fulladder_5 (.a(a_5), .b(b_5), .c(fulladder_4_carry), .sum(out_5), .carry(fulladder_5_carry));
  fulladder fulladder_6 (.a(a_6), .b(b_6), .c(fulladder_5_carry), .sum(out_6), .carry(fulladder_6_carry));
  fulladder fulladder_7 (.a(a_7), .b(b_7), .c(fulladder_6_carry), .sum(out_7), .carry(carry));
endmodule

module inc8 (
  input  a_0,
  input  a_1,
  input  a_2,
  input  a_3,
  input  a_4,
  input  a_5,
  input  a_6,
  input  a_7,
  output out_0,
  output out_1,
  output out_2,
  output out_3,
  output out_4,
  output out_5,
  output out_6,
  output out_7
);

  add8 add8_1 (
    .a_0(a_0), .a_1(a_1), .a_2(a_2), .a_3(a_3), .a_4(a_4), .a_5(a_5), .a_6(a_6), .a_7(a_7), .b_0(1'b1),
    .b_1(1'b0), .b_2(1'b0), .b_3(1'b0), .b_4(1'b0), .b_5(1'b0), .b_6(1'b0), .b_7(1'b0), .out_0(out_0),
    .out_1(out_1), .out_2(out_2), .out_3(out_3), .out_4(out_4), .out_5(out_5), .out_6(out_6), .out_7(out_7));  // open: carry
endmodule

module mux (
  input  a,
  input  b,
  input  sel,
  output out
);

  wire and_1_out, and_2_out, not_1_out;

  not not_1 (not_1_out, sel);
  and and_1 (and_1_out, a, not_1_out);
  and and_2 (and_2_out, b, sel);
  or or_1 (out, and_1_out, and_2_out);
endmodule

module mux8 (
  input  sel,
  input  a_0,
  input  b_0,
  input  a_1,
  input  b_1,
  input  a_2,
  input  b_2,
  input  a_3,
  input  b_3,
  input  a_4,
  input  b_4,
  input  a_5,
  input  b_5,
  input  a_6,
  input  b_6,
  input  a_7,
  input  b_7,
  output out_0,
  output out_1,
  output out_2,
  output out_3,
  output out_4,
  output out_5,
  output out_6,
  output out_7
);

  mux mux_1 (.a(a_0), .b(b_0), .sel(sel), .out(out_0));
  mux mux_2 (.a(a_1), .b(b_1), .sel(sel), .out(out_1));
  mux mux_3 (.a(a_2), .b(b_2), .sel(sel), .out(out_2));
  mux mux_4 (.a(a_3), .b(b_3), .sel(sel), .out(out_3));
  mux mux_5 (.a(a_4), .b(b_4), .sel(sel), .out(out_4));
  mux mux_6 (.a(a_5), .b(b_5), .sel(sel), .out(out_5));
  mux mux_7 (.a(a_6), .b(b_6), .sel(sel), .out(out_6));
  mux mux_8 (.a(a_7), .b(b_7), .sel(sel), .out(out_7));
endmodule

module \bit  (
  input  clock,
  input  in,
  input  load,
  output out
);

  wire dff_1_out_3, mux_1_out;

  dff dff_1 (.clock(clock), .in(mux_1_out), .out_3(dff_1_out_3), .out_4(out));
  mux mux_1 (.a(dff_1_out_3), .b(in), .sel(load), .out(mux_1_out));
endmodule

module dff (
  input  clock,
  input  in,
  output out_3,
  output out_4
);

  wire and_1_out, and_2_out, not_1_out;

  not not_1 (not_1_out, in);
  and and_1 (and_1_out, not_1_out, clock);
  and and_2 (and_2_out, clock, in);
  nor nor_1 (out_3, and_1_out, out_4);
  nor nor_2 (out_4, out_3, and_2_out);
endmodule

module \reg  (
  input  clock,
  input  load,
  input  in_0,
  input  in_1,
  input  in_2,
  input  in_3,
  input  in_4,
  input  in_5,
  input  in_6,
  input  in_7,
  output out_0,
  output out_1,
  output out_2,
  output out_3,
  output out_4,
  output out_5,
  output out_6,
  output out_7
);

  \bit  bit_1 (.clock(clock), .in(in_0), .load(load), .out(out_0));
  \bit  bit_2 (.clock(clock), .in(in_1), .load(load), .out(out_1));
  \bit  bit_3 (.clock(clock), .in(in_2), .load(load), .out(out_2));
  \bit  bit_4 (.clock(clock), .in(in_3), .load(load), .out(out_3));
  \bit  bit_5 (.clock(clock), .in(in_4), .load(load), .out(out_4));
  \bit  bit_6 (.clock(clock), .in(in_5), .load(load), .out(out_5));
  \bit  bit_7 (.clock(clock), .in(in_6), .load(load), .out(out_6));
  \bit  bit_8 (.clock(clock), .in(in_7), .load(load), .out(out_7));
endmodule
